# Fritzing sketch circuit (saved by Fritzing 0.9.9b)
breadboards: 1

parts:
  HC-SR04_Sensor_1 = HC-SR04 Ultrasonic Distance Sensor
  LCD1 = LCD screen
  J1 = STM32 Nucleo boards
  Componente1 = HX711 Weighing Sensor Module
  J2 = Basic Servo
  Load_Cell1 = Load Cell - Red/white/black/green

nets:
  VCC: HC-SR04_Sensor_1.VCC, LCD1.VDD, LCD1.LED+, J1.5V, Componente1.VCC, J2.vcc
  N1: HC-SR04_Sensor_1.TRIG, J1.D2
  N2: HC-SR04_Sensor_1.ECHO, J1.D1/TX
  GND: HC-SR04_Sensor_1.GND, LCD1.VSS, LCD1.R/W, LCD1.LED-, J1.GND, Componente1.GND, J2.gnd
  N3: LCD1.V0, J1.D3_PWM
  N4: LCD1.RS, J1.D4
  N5: LCD1.E, J1.D5_PWM
  N6: LCD1.DB4, J1.D10_PWM/SS
  N7: LCD1.DB5, J1.D11_PWM/MOSI
  N8: LCD1.DB6, J1.D12/MISO
  N9: LCD1.DB7, J1.D13/SCK
  N10: J1.D8, Componente1.DO/RX
  N11: J1.D9_PWM, Componente1.CK/TX
  N12: J1.PA15, J2.pulse
  N13: Componente1.E+, Load_Cell1.wire1
  N14: Componente1.E-, Load_Cell1.wire3
  N15: Componente1.A+, Load_Cell1.wire2
  N16: Componente1.A-, Load_Cell1.wire4

custom parts:
  Load Cell - Red/white/black/green: A rectangle load cell/weighting pressure Sensor with four wires - Red, white, black, green. Normally corresponding with E+, E-, A+, A- respectively.
